# Fritzing sketch NMEA-Wifi (saved by Fritzing 0.9.3b)
circuit board: 8.46667cm x 5.64444cm
breadboards: 1

parts:
  D1 = Rectifier Diode [part_number=1N4007 package="300 mil [THT]"]
  Q1 = PNP-Transistor [package="TO92 [THT]"]
  R2 = Resistor [tolerance=±5% resistance=1.5k package=THT]
  Q2 = NPN-Transistor [package="TO92 [THT]"]
  R3 = Resistor [tolerance=±5% resistance=820 package=THT]
  WeMos_D1_Mini1 = WeMos D1 Mini
  Power_plug1 = Power plug [part_number=5V]
  JP1 = Header 3 [package=screwterminal-3.5mm-3_lock.007s]
  R1 = Resistor [tolerance=±5% resistance=4.7k package=THT]

nets:
  N1: D1.cathode, Q1.E, JP1.RX-
  N2: D1.anode, Q1.B, R1.Pin_1
  N3: Q1.C, R2.Pin_0
  N4: R2.Pin_1, Q2.B
  GND: Q2.E, JP1.GND
  N5: Q2.C, R3.Pin_1, WeMos_D1_Mini1.D5
  N6: R3.Pin_0, WeMos_D1_Mini1.3V3
  5V: WeMos_D1_Mini1.5V, Power_plug1.VCC
  N7: WeMos_D1_Mini1.G, Power_plug1.GND
  N8: JP1.RX+, R1.Pin_0

notes:
  Rx+
  Rx-
  Gnd
  +3.3V

custom parts:
  Header 3: Header 3 Standard 3-pin 0.1 header. Use with straight break away headers (SKU : PRT-00116), right angle break away headers (PRT-00553), swiss pins (PRT-00743), machine pins (PRT-00117), and female headers (PRT-00115). Molex polarized connector foot print use with SKU : PRT-08232 with associated crimp pins and housings.
